# Fritzing sketch Doniczka (saved by Fritzing 1.0.6)
breadboards: 1

parts:
  Adafruit_INA237_85V_10A_16-bit_DC_Current_Voltage_Power_Monitor_-_STEMMA_QT1 = Adafruit INA237 85V 10A 16-bit DC Current Voltage Power Monitor - STEMMA QT [mn=Adafruit mpn=#6340 part_number=#6340]
  Chirp!_Soil_Moisture_Sensor1 = Chirp! Soil Moisture Sensor v2.7.3
  KY-1 = Keyes Relay [package=THT]
  M1 = DC Motor [voltage_(max)=6V voltage_(min)=3V]
  Power_plug1 = Power plug
  Raspberry_Pi_1 = Raspberry Pi 3 [part_number=RPI-3-V1.2]

nets:
  GND: Adafruit_INA237_85V_10A_16-bit_DC_Current_Voltage_Power_Monitor_-_STEMMA_QT1.GND, KY-1.ground, Raspberry_Pi_1.GND
  VCC: Adafruit_INA237_85V_10A_16-bit_DC_Current_Voltage_Power_Monitor_-_STEMMA_QT1.VCC, Raspberry_Pi_1.3v3
  N1: Adafruit_INA237_85V_10A_16-bit_DC_Current_Voltage_Power_Monitor_-_STEMMA_QT1.SCL, Chirp!_Soil_Moisture_Sensor1.pin_2, Raspberry_Pi_1.GPIO3
  N2: Adafruit_INA237_85V_10A_16-bit_DC_Current_Voltage_Power_Monitor_-_STEMMA_QT1.SDA, Chirp!_Soil_Moisture_Sensor1.pin_3, Raspberry_Pi_1.GPIO2
  N3: KY-1.signal, Raspberry_Pi_1.GPIO17
  N4: KY-1.power, Raspberry_Pi_1.GPIO8
  N5: KY-1.C, Power_plug1.VCC
  N6: KY-1.NO, M1.pin_1
  N7: M1.pin_2, Power_plug1.GND

custom parts:
  Keyes Relay: The Keyes 5V relay module is suitable for SCM development, home appliance control. It uses a 5V~12V TIL control signal which can control DC / AC signal.
